# Fritzing sketch 01_-_Analog_example (saved by Fritzing 0.9.3b)
breadboards: 1

parts:
  Part1 = Arduino Uno (Rev3) - ICSP
  U1 = POT [package=pot_mammoth]
  R1 = Resistor [tolerance=±5% resistance=220 package="0603 [SMD]"]
  U2 = POT [package=pot_mammoth]
  R2 = Resistor [tolerance=±5% resistance=220 package="0603 [SMD]"]
  J1 = Basic Force Sensing Resistor (FSR) [package=THT]
  R3 = Photocell (LDR) [package=THT]
  R4 = Resistor [tolerance=±5% resistance=10k package="0603 [SMD]"]
  R5 = Resistor [tolerance=±5% resistance=10k package="0603 [SMD]"]

nets:
  N1: Part1.A0, R1.Pin_0
  N2: Part1.A1, R2.Pin_0
  N3: Part1.A2, R3.pin_0, R4.Pin_1
  N4: Part1.A3, J1.pin_0, R5.Pin_1
  N5: Part1.5V, U1.S, U2.S, R4.Pin_0
  N6: Part1.GND, U1.E, U2.E, R3.pin_1, R5.Pin_0
  N7: U1.A, R1.Pin_1
  N8: U2.A, R2.Pin_1
